# Fritzing sketch assembly (saved by Fritzing 0.9.3b)
breadboards: 1

parts:
  U1 = NodeMCU V3.0

nets:
  N1: U1.GND#6, U1.GND#13, U1.GND#16, U1.GND#33

notes:
  SDA (28) -> D2 (13)
  SCL (27) -> D1 (14)
  3V (10) -> VCC (29)
  G (2)
  VU (13) -> VCC (21)
  GND -> GND (22)
  D7 (6) -> DIN (23)
  D4 (11) -> CS (24)
  D5 (8) -> CLK (25)

custom parts:
  NodeMCU V3.0: ESP8266 based NodeMCU
