# Fritzing sketch logical (saved by Fritzing 0.9.3b)

parts:
  U1 = NodeMCU V3.0
  ZS-042_RTC1 = ZS-042 RTC Module
  Part8 = LED Matrix - Serial Interface - Red/Green/Blue

nets:
  N1: U1.D1, ZS-042_RTC1.SCL
  N2: U1.D2, ZS-042_RTC1.SDA
  N3: U1.D4, Part8.CS
  3V3: U1.3V3, ZS-042_RTC1.VCC
  GND: U1.GND, ZS-042_RTC1.GND, Part8.GND
  N4: U1.D5, Part8.SCK
  N5: U1.D7, Part8.MISO
  N6: U1.VU, Part8.VCC

notes:
  Remember to remove the 201 resistor!
  CS
  DIN
  CLK
  VCC
  GND
  x4

custom parts:
  NodeMCU V3.0: ESP8266 based NodeMCU
