# Fritzing sketch led-matrix (saved by Fritzing 0.9.3b)

parts:
  Part1 = LED Matrix - Serial Interface - Red/Green/Blue
  Part2 = LED Matrix - Serial Interface - Red/Green/Blue
  Part3 = LED Matrix - Serial Interface - Red/Green/Blue
  Part4 = LED Matrix - Serial Interface - Red/Green/Blue
  U1 = NodeMCU V3.0

nets:
  VCC: Part1.VCC, Part2.VCC, Part3.VCC, Part4.VCC, U1.VU
  N1: Part1.SCK, Part2.SCK, Part3.SCK, Part4.SCK, U1.D5
  N2: Part1.CS, Part2.CS, Part3.CS, Part4.CS, U1.D4
  N3: Part1.MISO, U1.D7
  GND: Part1.GND, Part2.GND, Part3.GND, Part4.GND, U1.GND
  N4: Part1.MOSI, Part2.MISO
  N5: Part2.MOSI, Part3.MISO
  N6: Part3.MOSI, Part4.MISO

notes:
  CLK
  DIN
  CS

custom parts:
  NodeMCU V3.0: ESP8266 based NodeMCU
