# Fritzing sketch real-time-clock (saved by Fritzing 0.9.3b)

parts:
  U1 = NodeMCU V3.0
  ZS-042_RTC1 = ZS-042 RTC Module

nets:
  N1: U1.D1, ZS-042_RTC1.SCL
  N2: U1.D2, ZS-042_RTC1.SDA
  3V3: U1.3V3, ZS-042_RTC1.VCC
  GND: U1.GND, ZS-042_RTC1.GND

notes:
  Remember to remove the 201 resistor

custom parts:
  NodeMCU V3.0: ESP8266 based NodeMCU
